// Logisim project task1.circ as structural Verilog: 1 circuit, main circuit main
module main (
  input  \А ,
  input  B,
  input  C,
  output out_4,
  output out_5
);

  wire _2_out, _21_out, and_1_out, and_2_out, and_4_out, not_1_out, not_2_out, not_3_out, or_1_out, or_2_out,
       or_3_out, or_4_out, or_5_out, or_6_out, or_7_out, or_8_out;

  not not_1 (not_1_out, \А );
  not not_2 (not_2_out, B);
  not not_3 (not_3_out, C);
  or _2 (_2_out, C, not_2_out);
  or or_1 (or_1_out, \А , C);
  or or_2 (or_2_out, not_2_out, not_3_out);
  or or_3 (or_3_out, B, not_3_out);
  or or_4 (or_4_out, B, C);
  or _21 (_21_out, \А , B);
  or or_5 (or_5_out, \А , or_4_out);
  or or_6 (or_6_out, not_1_out, or_3_out);
  or or_7 (or_7_out, or_2_out, \А );
  or or_8 (or_8_out, not_1_out, _2_out);
  and and_1 (and_1_out, or_1_out, or_4_out);
  and and_2 (and_2_out, or_8_out, or_7_out);
  and and_3 (out_4, and_1_out, _21_out);
  and and_4 (and_4_out, and_2_out, or_6_out);
  and and_5 (out_5, or_5_out, and_4_out);

  // Notes on the sheet:
  //   3
  //   1
  //   5
  //   18
  //   7
  //   11
  //   16
  //   15
  //   5
  //   13
  //   8
  //   4
  //   20
  //   9
  //   22
  //   14
  //   P
  //   17
  //   S
endmodule
